# Fritzing sketch top_shelf_circuit (saved by Fritzing 0.9.3b)
breadboards: 2

parts:
  IC1 = DIP - 16 pins [chip_label="4051 (write)" package="DIP (Dual Inline) [THT]"]
  IC2 = DIP - 16 pins [chip_label="4051 (read)" package="DIP (Dual Inline) [THT]"]
  IC3 = DIP - 16 pins [chip_label="4051 (write)" package="DIP (Dual Inline) [THT]"]
  IC4 = DIP - 16 pins [chip_label="4051 (read)" package="DIP (Dual Inline) [THT]"]
  IC5 = DIP - 16 pins [chip_label="4051 (knobs)" package="DIP (Dual Inline) [THT]"]
  IC6 = DIP - 16 pins [chip_label="4051 (selector)" package="DIP (Dual Inline) [THT]"]
  R1 = Resistor [tolerance=±5% resistance=10k package=THT]
  R2 = Resistor [tolerance=±5% resistance=10k package=THT]
  Part1 = Arduino Mega 2560 (Rev3)
  IC7 = DIP - 16 pins [chip_label="4051 (write)" package="DIP (Dual Inline) [THT]"]
  IC8 = DIP - 16 pins [chip_label="4051 (write)" package="DIP (Dual Inline) [THT]"]
  IC9 = DIP - 16 pins [chip_label="4051 (read)" package="DIP (Dual Inline) [THT]"]
  IC10 = DIP - 16 pins [chip_label="4051 (read)" package="DIP (Dual Inline) [THT]"]
  IC11 = DIP - 16 pins [chip_label="4051 (knobs)" package="DIP (Dual Inline) [THT]"]
  R3 = Resistor [tolerance=±5% resistance=10k package=THT]
  R4 = Resistor [tolerance=±5% resistance=10k package=THT]

nets:
  N1: IC1.pin1, IC2.pin1
  N2: IC1.pin2, IC2.pin2
  N3: IC1.pin3, IC6.pin1
  N4: IC1.pin4, IC2.pin4
  N5: IC1.pin5, IC2.pin5
  N6: IC1.pin6, IC1.pin7, IC1.pin8, IC2.pin6, IC2.pin7, IC2.pin8, IC3.pin6, IC3.pin7, IC3.pin8, IC4.pin6, IC4.pin7, IC4.pin8, IC5.pin6, IC5.pin7, IC5.pin8, IC6.pin6, IC6.pin7, IC6.pin8, R1.Pin_1, R2.Pin_1, Part1.GND, IC7.pin6, IC7.pin7, IC7.pin8, IC8.pin6, IC8.pin7, IC8.pin8, IC9.pin6, IC9.pin7, IC9.pin8, IC10.pin6, IC10.pin7, IC10.pin8, IC11.pin6, IC11.pin7, IC11.pin8, R3.Pin_1, R4.Pin_1
  N7: IC1.pin9, IC3.pin9, Part1.D5_PWM, IC7.pin9, IC8.pin9
  N8: IC1.pin10, IC3.pin10, Part1.D6_PWM, IC7.pin10, IC8.pin10
  N9: IC1.pin11, IC3.pin11, Part1.D7_PWM, IC7.pin11, IC8.pin11
  N10: IC1.pin12, IC2.pin12
  N11: IC1.pin13, IC2.pin13
  N12: IC1.pin14, IC2.pin14
  N13: IC1.pin15, IC2.pin15
  N14: IC1.pin16, IC2.pin16, IC3.pin16, IC4.pin16, IC5.pin16, IC6.pin3, IC6.pin16, Part1.5V, IC7.pin16, IC8.pin16, IC9.pin16, IC10.pin16, IC11.pin16
  N15: IC2.pin3, R1.Pin_0, Part1.D22
  N16: IC2.pin9, IC4.pin9, IC5.pin9, Part1.D2_PWM, IC9.pin9, IC10.pin9, IC11.pin9
  N17: IC2.pin10, IC4.pin10, IC5.pin10, Part1.D3_PWM, IC9.pin10, IC10.pin10, IC11.pin10
  N18: IC2.pin11, IC4.pin11, IC5.pin11, Part1.D4_PWM, IC9.pin11, IC10.pin11, IC11.pin11
  N19: IC3.pin1, IC4.pin1
  N20: IC3.pin2, IC4.pin2
  N21: IC3.pin3, IC6.pin2
  N22: IC3.pin4, IC4.pin4
  N23: IC3.pin5, IC4.pin5
  N24: IC3.pin12, IC4.pin12
  N25: IC3.pin13, IC4.pin13
  N26: IC3.pin14, IC4.pin14
  N27: IC3.pin15, IC4.pin15
  N28: IC4.pin3, R2.Pin_0, Part1.D23
  N29: IC5.pin3, Part1.A0
  N30: IC6.pin4, IC8.pin3
  N31: IC6.pin5, IC7.pin3
  N32: IC6.pin9, Part1.D8_PWM
  N33: IC6.pin10, Part1.D9_PWM
  N34: IC6.pin11, Part1.D10_PWM
  N35: Part1.A1, IC11.pin3
  N36: Part1.D24, IC10.pin3, R3.Pin_0
  N37: Part1.D25, IC9.pin3, R4.Pin_0
  N38: IC7.pin1, IC9.pin1
  N39: IC7.pin2, IC9.pin2
  N40: IC7.pin4, IC9.pin4
  N41: IC7.pin5, IC9.pin5
  N42: IC7.pin12, IC9.pin12
  N43: IC7.pin13, IC9.pin13
  N44: IC7.pin14, IC9.pin14
  N45: IC7.pin15, IC9.pin15
  N46: IC8.pin1, IC10.pin1
  N47: IC8.pin2, IC10.pin2
  N48: IC8.pin4, IC10.pin4
  N49: IC8.pin5, IC10.pin5
  N50: IC8.pin12, IC10.pin12
  N51: IC8.pin13, IC10.pin13
  N52: IC8.pin14, IC10.pin14
  N53: IC8.pin15, IC10.pin15

custom parts:
  DIP - 16 pins: A DIP stand-in part for whatever IC you want. With 16 pins on a 300mil dual inline package (DIP) footprint.
